# Fritzing sketch Untitled Sketch (saved by Fritzing 0.9.3b)
circuit board: 8.46667cm x 5.64444cm
breadboards: 1

parts:
  Componente2 = Bluetooth HC-05 Macho
  KY-1 = Keyes Relay [package=THT]
  Componente3 = Arduino Mega ADK (Rev3)
  Componente4 = Bluetooth HC-05 Macho  # not connected
  KY-2 = Keyes Relay [package=THT]  # not connected
  Componente5 = Arduino Mega 2560 (Rev3)  # not connected

nets (from the breadboard view):
  N1: Componente2.TXD, Componente3.D0/RX0
  N2: Componente2.RXD, Componente3.D1/TX0
  VCC: Componente2.VCC, KY-1.power, Componente3.IOREF, Componente3.5V
  GND: Componente2.GND, KY-1.ground, Componente3.GND
  N3: KY-1.signal, Componente3.D2_PWM

custom parts:
  Keyes Relay: The Keyes 5V relay module is suitable for SCM development, home appliance control. It uses a 5V~12V TIL control signal which can control DC / AC signal.
